# Fritzing sketch schematics (saved by Fritzing 0.9.3b)

parts:
  Componente1 = Arduino Nano (Rev3.0) (ICSP)
  DI1 = 7-Segment LED Display [package=THT]
  R1 = Rotary Potentiometer (Small) [maximum_resistance=100kΩ package=THT]
  S1 = Round Pushbutton  # not connected
  J1 = Piezo Speaker  # not connected
  LED1 = smd LED [color="Red (633nm)" package="1206 [SMD]"]
  R2 = Resistor [tolerance=±5% resistance=220 package="2010 [SMD]"]
  R3 = Resistor [tolerance=±5% resistance=220 package="2010 [SMD]"]

nets:
  N1: Componente1.GND, R1.leg1, LED1.cathode, R2.Pin_1
  N2: Componente1.D2, DI1.cathodeC
  N3: Componente1.D3, DI1.cathodeD
  N4: Componente1.D4, DI1.cathodeE
  N5: Componente1.D5, DI1.cathodeB
  N6: Componente1.D6, DI1.cathodeA
  N7: Componente1.D7, DI1.cathodeF
  N8: Componente1.D8, DI1.cathodeG
  N9: Componente1.D10, R3.Pin_0
  N10: Componente1.5V, R1.leg2
  N11: Componente1.A0, R1.wiper
  N12: DI1.commAnode, R2.Pin_0
